# Fritzing sketch rosetta_Schematics_PCB (saved by Fritzing 0.9.3b)
circuit board: 13.1929cm x 12.9895cm

parts:
  10000_Mah = Battery Holders [package=lipo-1100mAh]
  Raspberry_pi_5 = Raspberry Pi 5
  Stop_button = SWITCH-MOMENTARY-2 [package=tactile_switch_smd-2]
  Distance = Adafruit VL530X Time of Flight Distance Sensor [part_number="Adafruit #3317"]
  Start_button = SWITCH-MOMENTARY-2 [package=tactile_switch_smd-2]
  Seeed_Respeaker = INMP441  # not connected
  Light = VEML6070 [part_number=VEML6070]
  U1 = ESP32-38PinWide [part_number=ESP32-38PinWide]
  charger_adaptor = PowerBoost 500 Charger
  Temp_Humidity_&_Pressure = Adafruit BME280 [part_number="Adafruit #2652"]
  CO2_Sensor = Adafruit SGP30 Gas Sensor
  LED1 = LED - 3mm [color="Red (633nm)" package="3 mm [THT]"]
  R1 = Resistor [tolerance=±5% resistance=220 package=THT]

nets:
  N1: 10000_Mah.+, charger_adaptor.VBAT_IN
  N2: 10000_Mah.-, charger_adaptor.GND_BAT_IN
  5V: Raspberry_pi_5.5V, Raspberry_pi_5.Fan-5V, U1.VIN, charger_adaptor.5.0V
  GND: Raspberry_pi_5.GND, Raspberry_pi_5.Fan-GND, Stop_button.2, Distance.GND, Start_button.2, Light.GND, U1.GND, charger_adaptor.GND, Temp_Humidity_&_Pressure.GND, CO2_Sensor.GND, R1.Pin_0
  N3: Raspberry_pi_5.ID_SC, LED1.cathode
  N4: Raspberry_pi_5.GPIO12, Start_button.1
  N5: Raspberry_pi_5.GPIO26, Stop_button.1
  VCC: Distance.VCC, Light.VDD, U1.3.3, Temp_Humidity_&_Pressure.VCC, CO2_Sensor.VIN
  N6: Distance.SDA, Light.SDA, U1.GPIO21, Temp_Humidity_&_Pressure.SDI/SDA, CO2_Sensor.SDA
  N7: Distance.SCL, Light.SCL, U1.GPIO22, Temp_Humidity_&_Pressure.SCK/SCL, CO2_Sensor.SCL
  N8: LED1.anode, R1.Pin_1

custom parts:
  Raspberry Pi 5: The RPi5, a faster version of the awesome Raspberry Pi4B ARM Board with 40 pin gpio.
  Adafruit VL530X Time of Flight Distance Sensor: The VL53L0X is a Time of Flight distance sensor like no other you've used! The sensor contains a very tiny invisible laser source, and a matching sensor. The VL53L0X can detect the "time of flight", or how long the light has taken to bounce back to the sensor. Since it uses a very narrow light source, it is good for determining distance of only the surface directly in front of it. Unlike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
  INMP441: This is a simple breakout board for the INMP441 I2S MEMS microphone.
  VEML6070: This little sensor is a great way to add UV light sensing to any microcontroller project. The VEML6070 from Vishay has a true UV A light sensor and an I2C-controlled ADC that will take readings and integrate them for you over ~60ms to 500ms.
  ESP32-38PinWide: Generic 38-Pin ESP32 with wide format (only access to one side of pins on a breadboard) based on Stephen Lilley's HiLetgo ESP-WROOM-32 ESP32 ESP-32S Development Board.
  Adafruit BME280: Bosch has stepped up their game with their new BME280 sensor, an environmental sensor with temperature, barometric pressure and humidity! This sensor is great for all sorts of weather/environmental sensing and can even be used in both I2C and SPI! This precision sensor from Bosch is the best low-cost sensing solution for measuring humidity with ±3% accuracy, barometric pressure with ±1 hPa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
